# Fritzing sketch schematick (saved by Fritzing 0.9.3b)
breadboards: 1

parts:
  S1 = Pushbutton [package="[THT]"]
  S2 = Pushbutton [package="[THT]"]
  S3 = Pushbutton [package="[THT]"]
  S4 = Pushbutton [package="[THT]"]
  S5 = Pushbutton [package="[THT]"]
  R1 = Resistor [tolerance=±5% resistance=220 package=THT]
  R2 = Resistor [tolerance=±5% resistance=220 package=THT]
  R3 = Resistor [tolerance=±5% resistance=220 package=THT]
  R4 = Resistor [tolerance=±5% resistance=220 package=THT]
  R5 = Resistor [tolerance=±5% resistance=220 package=THT]
  R6 = Resistor [tolerance=±5% resistance=220 package=THT]
  Part1 = Arduino Uno (Rev3)
  LCD1 = LCD screen  # not connected

nets:
  N1: S1.Pin_1, S1.Pin_2, R2.Pin_1
  N2: S1.Pin_3, S1.Pin_4, S2.Pin_3, S2.Pin_4, S3.Pin_3, S3.Pin_4, S4.Pin_3, S4.Pin_4, S5.Pin_3, S5.Pin_4, R1.Pin_1, Part1.A0
  N3: S2.Pin_1, S2.Pin_2, R4.Pin_0
  N4: S3.Pin_1, S3.Pin_2, R3.Pin_1
  N5: S4.Pin_1, S4.Pin_2, R5.Pin_1
  N6: S5.Pin_1, S5.Pin_2, R6.Pin_1
  N7: R1.Pin_0, Part1.GND
  N8: R2.Pin_0, R3.Pin_0, R4.Pin_1, R5.Pin_0, R6.Pin_0, Part1.5V
